# Fritzing sketch _BOARD_NodeMCU (saved by Fritzing 0.9.3b)
breadboards: 1

parts:
  U1 = NodeMCU V1.0
  ZS-042_RTC1 = ZS-042 RTC Module  # not connected
  R1 = Photocell (LDR) [package=THT]
  IR2 = TSOP312.., 314.. [part_number="IR Receiver TSOP31240" package=THT]
  J3 = female pin header, 4 pins [form="♀ (female)" part_number="DCF77 Header 3V3, GND, DATA, PON"]
  J4 = female pin header, 2 pins [form="♀ (female)" part_number="5 Volt in"]
  R9 = Resistor [tolerance=±5% resistance=10k package=THT]
  J5 = Piezo Speaker

nets:
  N1: U1.D4, IR2.Data
  N2: U1.3V3, IR2.Vs
  GND: U1.GND, R1.pin_1, IR2.GND, J3.pin3, J4.pin2, R9.Pin_1, J5.pin1
  N3: U1.D5, J5.pin2
  N4: U1.D7, J3.pin2
  N5: U1.D8, J3.pin1
  N6: U1.Vin, J3.pin4, J4.pin1
  N7: U1.A0, R1.pin_0, R9.Pin_0

notes:
  BOARD_NODEMCU
  5Vin
  3V3
  LED-Stripe Header:
  5V, GND, (CLOCK), DATA

custom parts:
  NodeMCU V1.0: ESP8266 based NodeMCU
